// Logisim project CARRYADDER.circ as structural Verilog: 3 circuits, main circuit main
module main (
  input  C0,
  input  [3:0] X,
  input  [3:0] Y,
  input  in_4
);

  wire and_1_out, and_2_out, and_3_out, and_4_out, and_5_out, and_6_out, and_7_out, and_8_out, and_9_out,
       and_10_out, gp_1_g, gp_1_p, gp_2_g, gp_2_p, gp_3_g, gp_3_p, gp_4_g, gp_4_p, or_1_out, or_2_out,
       or_3_out;
  wire [0:0] or_4_out;
  wire [3:0] fulladder_3_s;

  Hex_Digit_Display hex_digit_display_1 (.value({{3{in_4}}, or_4_out[0]}));  // open: dp
  Hex_Digit_Display hex_digit_display_2 (.value(fulladder_3_s));  // open: dp
  GP gp_1 (.X(X[1]), .Y(Y[1]), .P(gp_1_p), .G(gp_1_g));
  GP gp_2 (.X(X[2]), .Y(Y[2]), .P(gp_2_p), .G(gp_2_g));
  GP gp_3 (.X(X[3]), .Y(Y[3]), .P(gp_3_p), .G(gp_3_g));
  GP gp_4 (.X(X[0]), .Y(Y[0]), .P(gp_4_p), .G(gp_4_g));
  and and_1 (and_1_out, C0, gp_4_p);
  and and_2 (and_2_out, C0, gp_4_p, gp_1_p);
  and and_3 (and_3_out, gp_1_p, gp_4_g);
  and and_4 (and_4_out, gp_2_p, gp_1_p, gp_4_p, C0);
  and and_5 (and_5_out, gp_2_p, gp_1_p, gp_4_g);
  and and_6 (and_6_out, gp_2_p, gp_1_g);
  and and_7 (and_7_out, gp_3_p, gp_2_p, gp_1_p, gp_4_p, C0);
  and and_8 (and_8_out, gp_3_p, gp_2_p, gp_1_p, gp_4_g);
  and and_9 (and_9_out, gp_3_p, gp_2_p, gp_1_g);
  and and_10 (and_10_out, gp_3_p, gp_2_g);
  or or_1 (or_1_out, and_1_out, gp_4_g);
  or or_2 (or_2_out, and_2_out, and_3_out, gp_1_g);
  or or_3 (or_3_out, and_4_out, and_5_out, and_6_out, gp_2_g);
  or or_4 (or_4_out[0], and_7_out, and_8_out, and_9_out, and_10_out, gp_3_g);
  fulladder fulladder_1 (.X(X[1]), .Y(Y[1]), .C(or_1_out), .S(fulladder_3_s[1]));
  fulladder fulladder_2 (.X(X[2]), .Y(Y[2]), .C(or_2_out), .S(fulladder_3_s[2]));
  fulladder fulladder_3 (.X(X[0]), .Y(Y[0]), .C(C0), .S(fulladder_3_s[0]));
  fulladder fulladder_4 (.X(X[3]), .Y(Y[3]), .C(or_3_out), .S(fulladder_3_s[3]));

  // Notes on the sheet:
  //   G1
  //   P2
  //   G2
  //   P3
  //   G3
  //   P0
  //   G0
  //   P1
endmodule

module fulladder (
  input  X,
  input  Y,
  input  C,
  output S
);

  wire xor_1_out;

  xor xor_1 (xor_1_out, X, Y);
  xor xor_2 (S, xor_1_out, C);
endmodule

module GP (
  input  X,
  input  Y,
  output P,
  output G
);

  xor xor_1 (P, X, Y);
  and and_1 (G, X, Y);
endmodule
