// Logisim project Universalshiftreg.circ as structural Verilog: 1 circuit, main circuit main
module main (
  input  [3:0] I,
  input  D,
  input  [1:0] Selectline,
  input  Set,
  input  Reset,
  output [3:0] O
);

  wire clock_1_out, multiplexer_1_out, multiplexer_2_out, multiplexer_3_out, multiplexer_4_out;

  Clock clock_1 (.out(clock_1_out));
  Multiplexer #(.select(2)) multiplexer_1 (
    .in0(D), .in1(O[1]), .in2(I[0]), .in3(O[0]), .out(multiplexer_1_out), .sel(Selectline));
  D_Flip_Flop d_ff_1 (.D(multiplexer_1_out), .clk(clock_1_out), .Q(O[0]), .preset(Set), .reset(Reset));  // open: Qn
  Multiplexer #(.select(2)) multiplexer_2 (
    .in0(O[0]), .in1(O[2]), .in2(I[1]), .in3(O[1]), .out(multiplexer_2_out), .sel(Selectline));
  D_Flip_Flop d_ff_2 (.D(multiplexer_2_out), .clk(clock_1_out), .Q(O[1]), .preset(Set), .reset(Reset));  // open: Qn
  Multiplexer #(.select(2)) multiplexer_3 (
    .in0(O[1]), .in1(O[3]), .in2(I[2]), .in3(O[2]), .out(multiplexer_3_out), .sel(Selectline));
  D_Flip_Flop d_ff_3 (.D(multiplexer_3_out), .clk(clock_1_out), .Q(O[2]), .preset(Set), .reset(Reset));  // open: Qn
  Multiplexer #(.select(2)) multiplexer_4 (
    .in0(O[2]), .in1(D), .in2(I[3]), .in3(O[3]), .out(multiplexer_4_out), .sel(Selectline));
  D_Flip_Flop d_ff_4 (.D(multiplexer_4_out), .clk(clock_1_out), .Q(O[3]), .preset(Set), .reset(Reset));  // open: Qn
endmodule
