// Logisim project cyclecounter.circ as structural Verilog: 1 circuit, main circuit main
module main (
  input  Set,
  input  Reset,
  input  Pause
);

  wire and_1_out, and_2_out, and_3_out, and_4_out, and_5_out, and_6_out, clock_1_out, not_1_out, not_2_out,
       not_3_out;
  wire [2:0] C_q;
  wire [3:0] t_ff_1_q;

  Clock clock_1 (.out(clock_1_out));
  not not_1 (not_1_out, Pause);
  and and_1 (and_1_out, not_3_out, not_1_out);
  T_Flip_Flop A (.T(and_2_out), .clk(clock_1_out), .Q(C_q[2]), .reset(Reset), .preset(Set));  // open: Qn
  and and_2 (and_2_out, not_2_out, and_1_out);
  T_Flip_Flop B (.T(and_1_out), .clk(clock_1_out), .Q(C_q[1]), .reset(Reset), .preset(Set));  // open: Qn
  T_Flip_Flop C (.T(not_1_out), .clk(clock_1_out), .Q(C_q[0]), .reset(Reset), .preset(Set));  // open: Qn
  T_Flip_Flop t_ff_1 (.T(and_3_out), .clk(clock_1_out), .Q(t_ff_1_q[0]), .reset(Reset), .preset(Set));  // open: Qn
  and and_3 (and_3_out, C_q[2], not_2_out, C_q[0]);
  not not_2 (not_2_out, C_q[1]);
  not not_3 (not_3_out, C_q[0]);
  T_Flip_Flop t_ff_2 (.T(and_4_out), .clk(clock_1_out), .Q(t_ff_1_q[1]), .reset(Reset), .preset(Set));  // open: Qn
  and and_4 (and_4_out, t_ff_1_q[0], and_3_out);
  and and_5 (and_5_out, and_3_out, t_ff_1_q[0], t_ff_1_q[1]);
  T_Flip_Flop t_ff_3 (.T(and_5_out), .clk(clock_1_out), .Q(t_ff_1_q[2]), .reset(Reset), .preset(Set));  // open: Qn
  T_Flip_Flop t_ff_4 (.T(and_6_out), .clk(clock_1_out), .Q(t_ff_1_q[3]), .reset(Reset), .preset(Set));  // open: Qn
  and and_6 (and_6_out, and_3_out, t_ff_1_q[0], t_ff_1_q[1], t_ff_1_q[2]);
  Hex_Digit_Display Mod8Counter (.value({1'b0, C_q}));  // open: dp
  Hex_Digit_Display cyclecounter (.value(t_ff_1_q));  // open: dp
endmodule
